// Digital circuit 32bit_IsZero.dig as structural Verilog
module _32bit_IsZero (
  input  [31:0] A,
  output O
);

  wire and_1_out, and_2_out, nor_1_out, nor_2_out, nor_3_out, nor_4_out, nor_5_out, nor_6_out, nor_7_out,
       nor_8_out;

  nor nor_1 (nor_1_out, A[0], A[1], A[2], A[3]);
  nor nor_2 (nor_2_out, A[4], A[5], A[6], A[7]);
  nor nor_3 (nor_3_out, A[8], A[9], A[10], A[11]);
  nor nor_4 (nor_4_out, A[12], A[13], A[14], A[15]);
  nor nor_5 (nor_5_out, A[16], A[17], A[18], A[19]);
  nor nor_6 (nor_6_out, A[20], A[21], A[22], A[23]);
  nor nor_7 (nor_7_out, A[24], A[25], A[26], A[27]);
  nor nor_8 (nor_8_out, A[28], A[29], A[30], A[31]);
  and and_1 (and_1_out, nor_1_out, nor_2_out, nor_3_out, nor_4_out);
  and and_2 (and_2_out, nor_5_out, nor_6_out, nor_7_out, nor_8_out);
  and and_3 (O, and_1_out, and_2_out);
endmodule
