// Digital circuit ALU.dig as structural Verilog
// The Arithmetic Logic Unit (ALU) component, which can perform various operations on the provided operands, also determining the resulting flag values.
module ALU (
  input  [31:0] B,
  input  [31:0] A,
  input  [2:0] Opcode,
  output [31:0] Result,
  output Carry,
  output Overflow,
  output Negative,
  output Zero
);

  wire add_1_c_o, msb_1_o, msb_2_o, msb_3_o, not_1_out, overflowadder_1_o, overflowsubtract_1_o,
       rotateleft_1_p4, shiftleft_1_p4, shiftright_1_p4, sub_1_c_o, xor_2_out, xor_3_out;
  wire [31:0] add_1_s, and_1_out, or_1_out, rotateleft_1_p3, shiftleft_1_p3, shiftright_1_p3, sub_1_s,
       xor_1_out;

  assign or_1_out = B | A;  // Or or_1, 32 bits wide
  assign xor_1_out = B ^ B;  // XOr xor_1, 32 bits wide
  assign and_1_out = B & A;  // And and_1, 32 bits wide
  // ShiftLeft shiftleft_1: pin names not known; wires that end beside it: A, B, shiftleft_1_p3, shiftleft_1_p4
  // ShiftRight shiftright_1: pin names not known; wires that end beside it: A, B, shiftright_1_p3, shiftright_1_p4
  // RotateLeft rotateleft_1: pin names not known; wires that end beside it: A, B, rotateleft_1_p3, rotateleft_1_p4
  Add #(.Bits(32)) add_1 (.a(A), .b(B), .c_i(1'b0), .s(add_1_s), .c_o(add_1_c_o));
  Sub #(.Bits(32)) sub_1 (.a(A), .b(B), .c_i(1'b0), .s(sub_1_s), .c_o(sub_1_c_o));
  MSB msb_1 (.A(shiftleft_1_p3), .O(msb_1_o));
  OverflowAdder overflowadder_1 (.A(B), .B(A), .Result(add_1_s), .O(overflowadder_1_o));
  OverflowSubtract overflowsubtract_1 (.A(A), .B(B), .Result(sub_1_s), .O(overflowsubtract_1_o));
  xor xor_2 (xor_2_out, msb_1_o, shiftleft_1_p4);
  MSB msb_2 (.A(rotateleft_1_p3), .O(msb_2_o));
  xor xor_3 (xor_3_out, msb_2_o, rotateleft_1_p4);
  MSB msb_3 (.A(B), .O(msb_3_o));
  Multiplexer #(.Selector_Bits(3), .Bits(32)) multiplexer_1 (
    .sel(Opcode), .in_0(or_1_out), .in_1(xor_1_out), .in_2(and_1_out), .in_3(shiftleft_1_p3),
    .in_4(shiftright_1_p3), .in_5(rotateleft_1_p3), .in_6(add_1_s), .in_7(sub_1_s), .out(Result));
  Multiplexer #(.Selector_Bits(3)) multiplexer_2 (
    .sel(Opcode), .in_0(1'b0), .in_1(1'b0), .in_2(1'b0), .in_3(xor_2_out), .in_4(msb_3_o), .in_5(xor_3_out),
    .in_6(overflowadder_1_o), .in_7(overflowsubtract_1_o), .out(Overflow));
  MSB msb_4 (.A(Result), .O(Negative));
  _32bit_IsZero _32bit_iszero_1 (.A(Result), .O(Zero));
  not not_1 (not_1_out, sub_1_c_o);
  Multiplexer #(.Selector_Bits(3)) multiplexer_3 (
    .sel(Opcode), .in_0(1'b0), .in_1(1'b0), .in_2(1'b0), .in_3(shiftleft_1_p4), .in_4(shiftright_1_p4),
    .in_5(rotateleft_1_p4), .in_6(add_1_c_o), .in_7(not_1_out), .out(Carry));

  // Notes on the sheet:
  //   B: The value of the ALU B operand.
  //   A: The value of the ALU A operand.
  //   Result: The resuling value, containing the value computed by the ALU.
  //   Carry: The resulting carry flag.
  //   Overflow: The resulting overflow flag.
  //   Negative: The resulting negative flag.
  //   Zero: The resulting zero flag.
  //   Opcode: The ALU opcode, which specifies the operation to perform.
  //   Positive - Negative = Negative
  //   Negative - Positive = Positive
  //   A - B = R
  //   A = R + B
  //   R + B = A
  //   A + B = R
  //   A = R
  //   R = A
endmodule

/* Test case Sub:
A B Opcode Result Carry Overflow Negative Zero

loop(i, 256)
    # determine random values for A and B inputs
    let a = random(1<<32);
    let b = random(1<<32);

    # compute expected Result
    let r = a + (~b & 0xffffffff) + 1;

    # determine expected flags
    let c = (r) >= (1<<32);
    let o = (((a>>31)&1) != ((b>>31)&1)) & (((a>>31)&1) != ((r>>31)&1));
    let n = (r>>31) & 1;
    let z = r=0;

    # perform subtraction, and then check Result and flags are as expected
    (a) (b) 7 (r) (c) (o) (n) (z)
end loop
*/

/* Test case Rol:
A B Opcode Result Carry Overflow Negative Zero

loop(i, 256)
    # determine random values for A and B inputs
    let a = random(1<<32);
    let b = random(1<<32);

    # compute expected Result
    let rot = a&31;
    let r = (b << rot) | (b >> (32-rot));

    # determine expected flags
    let c = ite(a = 0, 0, r & 1);
    let o = c != ((r>>31)&1);
    let n = (r>>31) & 1;
    let z = r=0;

    # perform rotation, and then check Result and flags are as expected
    (a) (b) 5 (r) (c) (o) (n) (z)
end loop

loop(i, 16)
    # determine random values for inputs
    # set A to 0 to test edge case for Carry flag
    let a = 0;
    let b = random(1<<32);

    # compute expected Result
    let rot = a&31;
    let r = (b << rot) | (b >> (32-rot));

    # determine expected flags
    let c = ite(a = 0, 0, r & 1);
    let o = c != ((r>>31)&1);
    let n = (r>>31) & 1;
    let z = r=0;

    # perform rotation, and then check Result and flags are as expected
    (a) (b) 5 (r) (c) (o) (n) (z)
end loop
*/

/* Test case Shr:
A B Opcode Result Carry Overflow Negative Zero

loop(i, 256)
    # determine random values for A and B inputs
    let a = random(1<<32) & 0x3f;
    let b = random(1<<32);

    # compute expected Result
    let r = ite((a >= 0 & a <= 32), ((b >> a) & 0xffffffff), 0);

    # determine expected flags
    let c = ite(a = 0 | a > 32, 0, (b >> (a-1)) & 1);
    let o = (b>>31) & 1;
    let n = (r>>31) & 1;
    let z = r=0;

    # perform logical shift right, and then check Result and flags are as expected
    (a) (b) 4 (r) (c) (o) (n) (z)
end loop
*/

/* Test case Shl:
A B Opcode Result Carry Overflow Negative Zero

loop(i, 256)
    # determine random values for A and B inputs
    let a = random(1<<32) & 0x3f;
    let b = random(1<<32);

    # compute expected Result
    let r = ite((a >= 0 & a <= 32), (b << a) & 0xffffffff, 0);

    # determine expected flags
    let c = ite(a = 0 | a > 32, 0, (b >> (32-a)) & 1);
    let o = c != ((r>>31)&1);
    let n = (r>>31) & 1;
    let z = r=0;

    # perform logical shift left, and then check Result and flags are as expected
    (a) (b) 3 (r) (c) (o) (n) (z)
end loop
*/
