// Digital circuit CPU.dig as structural Verilog
// The Radboud University Nijmegen Central Processing Unit (RUNCPU), which is a basic 32-bit CPU for the Processors course, part of the Computing Science Bachelor.
module CPU (
  input  Clock,
  input  [31:0] Databus_in,
  output [31:0] Addressbus,
  output [31:0] Databus_out,
  output RE,
  output WE,
  output Halted
);

  wire ALU_carry, ALU_negative, ALU_overflow, ALU_zero, and_1_out, and_2_out, FlagRegisterBank_carry_out,
       FlagRegisterBank_negative_out, FlagRegisterBank_overflow_out, FlagRegisterBank_zero_out,
       instructiondecoder_1_arith2, instructiondecoder_1_arith3, instructiondecoder_1_loadhi,
       instructiondecoder_1_setflag, not_1_out, or_1_out, Timer_p2, Timer_p3, Timer_p5, Timer_p6;
  wire [2:0] instructiondecoder_1_opcode;
  wire [3:0] instructiondecoder_1_condition, instructiondecoder_1_reg_a, instructiondecoder_1_reg_b,
       instructiondecoder_1_reg_dest;
  wire [31:0] ALU_result, instructiondecoder_1_constant, multiplexer_1_out, multiplexer_2_out,
       multiplexer_3_out, RegisterBank_p7;

  // Timer Timer: pin names not known; wires that end beside it: Clock, Timer_p2, Timer_p3, Halted, Timer_p5, Timer_p6
  InstructionDecoder instructiondecoder_1 (
    .Instruction(Databus_in), .Fetch(Timer_p5), .Execute(Timer_p6), .Clock(Clock),
    .Reg_dest(instructiondecoder_1_reg_dest), .Reg_B(instructiondecoder_1_reg_b),
    .Reg_A(instructiondecoder_1_reg_a), .Opcode(instructiondecoder_1_opcode),
    .Condition(instructiondecoder_1_condition), .SetFlag(instructiondecoder_1_setflag),
    .Constant(instructiondecoder_1_constant), .Halt(Timer_p3), .WE(WE), .RE(RE),
    .LOADHI(instructiondecoder_1_loadhi), .ARITH2(instructiondecoder_1_arith2),
    .ARITH3(instructiondecoder_1_arith3));
  and and_1 (and_1_out, RE, ~Timer_p5);  // And
  Multiplexer #(.Bits(32)) multiplexer_1 (
    .sel(and_1_out), .in_0(ALU_result), .in_1(Databus_in), .out(multiplexer_1_out));
  not not_1 (not_1_out, RE);
  and and_2 (and_2_out, not_1_out, instructiondecoder_1_loadhi);
  Multiplexer #(.Bits(32)) multiplexer_2 (
    .sel(and_2_out), .in_0(multiplexer_1_out), .in_1(instructiondecoder_1_constant), .out(multiplexer_2_out));
  // RegisterBank RegisterBank: pin names not known; wires that end beside it: instructiondecoder_1_arith3, multiplexer_2_out, instructiondecoder_1_reg_dest, instructiondecoder_1_reg_b, instructiondecoder_1_reg_a, Clock, RegisterBank_p7, Databus_out
  or or_1 (or_1_out, WE, RE, instructiondecoder_1_loadhi, instructiondecoder_1_arith2);
  Multiplexer #(.Bits(32)) multiplexer_3 (
    .sel(or_1_out), .in_0(Databus_out), .in_1(instructiondecoder_1_constant), .out(multiplexer_3_out));
  ALU ALU (
    .B(RegisterBank_p7), .A(multiplexer_3_out), .Opcode(instructiondecoder_1_opcode), .Result(ALU_result),
    .Carry(ALU_carry), .Overflow(ALU_overflow), .Negative(ALU_negative), .Zero(ALU_zero));
  Multiplexer #(.Bits(32)) multiplexer_4 (.sel(Timer_p5), .in_0(ALU_result), .in_1(RegisterBank_p7), .out(Addressbus));
  FlagRegisterBank FlagRegisterBank (
    .Carry_in(ALU_carry), .Overflow_in(ALU_overflow), .Negative_in(ALU_negative), .Zero_in(ALU_zero),
    .Set(instructiondecoder_1_setflag), .Clock(Clock), .Carry_out(FlagRegisterBank_carry_out),
    .Overflow_out(FlagRegisterBank_overflow_out), .Negative_out(FlagRegisterBank_negative_out),
    .Zero_out(FlagRegisterBank_zero_out));
  Tester Tester (
    .Carry(FlagRegisterBank_carry_out), .Overflow(FlagRegisterBank_overflow_out),
    .Negative(FlagRegisterBank_negative_out), .Zero(FlagRegisterBank_zero_out),
    .Condition(instructiondecoder_1_condition), .TestSucceeds(Timer_p2));

  // Notes on the sheet:
  //   Addressbus: The addressbus signal, which determines the address of a read or write operation. For a write operation the address is where a value being written by the CPU should be stored. For a read operation the address is where a value being read by the CPU should be read from.
  //   Databus_out: The databus signal from the CPU. Any values written by the CPU will be stored here.
  //   RE: Read enabled signal. When a read operation is performed by the CPU this value is set to high.
  //   WE: Write enabled signal. When a write operation is performed by the CPU this value is set to high.
  //   Halted: Determines whether the CPU is in the halted state, in which it shall remain until the CPU is restarted.
  //   Databus_in: The databus signal to the CPU. Any values read (or instructions fetched) by the CPU will be stored here.
endmodule

/* Test case init:
Clock Databus_in Halted RE WE Databus_out Addressbus
0     0          0      1  0  x           0
*/

/* Test case add:
Clock Databus_in Halted RE WE Databus_out Addressbus R3
# The first line of test data must be the header, which contains the inputs and outputs used in the test case.
# It is possible to use registers in test cases by enabling their 'use as measurement value' attribute in the advanced tab.
# The R0-R15 registers have this attribute enabled in the provided template.

# These init statements are used to set the register contents when the simulation is started.
# Note that all init statements are collected and executed first. Interleaving them with regular test data has no effect.
# If you wish to test other instructions, or with different values, you must add a new test case component to the circuit.
# If you do not do this, the tests will run sequentially, meaning the next test will use the CPU state obtained after executing the prior test.
# This is reflected below in the last test data row that checks if the program counter increased by 4.
init R1=4;
init R2=5;

# ADD R1, R2, R3
# The four test data lines below describe the testing of the ADD R1, R2, R3 instruction.
# We first load the machine code into the Databus_in, and then drive the clock to step through the full instruction cycle once.
# Note that the first two columns (in this case) are inputs, meaning they will be set to the provided value.
# The other columns are outputs, which are evaluated after the inputs have been set, and then compared against the given expected values.
# The value 'x' denotes a 'do not care' value. Please click the 'Help' button in this dialog for more information regarding test cases.
0     0x6400123f 0      1  0  x           0          x
1     0x6400123f 0      x  x  x           x          x
0     0          0      0  0  x           x          x
1     0          0      0  0  x           x          9

# Fetch next instruction, check if the program counter increased by 4...
0     0          0      1  0  x           4          x
*/

/* Test case add and write:
Clock Databus_in Halted RE WE Databus_out Addressbus R3
# The first line of test data must be the header, which contains the inputs and outputs used in the test case.
# It is possible to use registers in test cases by enabling their 'use as measurement value' attribute in the advanced tab.
# The R0-R15 registers have this attribute enabled in the provided template.

# These init statements are used to set the register contents when the simulation is started.
# Note that all init statements are collected and executed first. Interleaving them with regular test data has no effect.
# If you wish to test other instructions, or with different values, you must add a new test case component to the circuit.
# If you do not do this, the tests will run sequentially, meaning the next test will use the CPU state obtained after executing the prior test.
# This is reflected below in the last test data row that checks if the program counter increased by 4.
init R1=4;
init R2=5;

# ADD R1, R2, R3
# The four test data lines below describe the testing of the ADD R1, R2, R3 instruction.
# We first load the machine code into the Databus_in, and then drive the clock to step through the full instruction cycle once.
# Note that the first two columns (in this case) are inputs, meaning they will be set to the provided value.
# The other columns are outputs, which are evaluated after the inputs have been set, and then compared against the given expected values.
# The value 'x' denotes a 'do not care' value. Please click the 'Help' button in this dialog for more information regarding test cases.
0     0x6400123f 0      1  0  x           0          x
1     0x6400123f 0      x  x  x           x          x
0     0          0      0  0  x           x          x
1     0          0      0  0  x           x          9

# Fetch next instruction, check if the program counter increased by 4...
0     0          0      1  0  x           4          x

# WRITE R3, [R0 + 216]
0     0xe0d8300f 0      1  0  x           4          x
1     0xe0d8300f 0      x  x  x           x          x
0     0          0      0  1  9           0xd8       x
1     0          0      0  0  x           x          x

# Fetch next instruction, check if the program counter increased by 4...
0     0          0      1  0  x           8          x
*/

/* Test case write:
Clock Databus_in Halted RE WE Databus_out Addressbus R3
# The first line of test data must be the header, which contains the inputs and outputs used in the test case.
# It is possible to use registers in test cases by enabling their 'use as measurement value' attribute in the advanced tab.
# The R0-R15 registers have this attribute enabled in the provided template.

# These init statements are used to set the register contents when the simulation is started.
# Note that all init statements are collected and executed first. Interleaving them with regular test data has no effect.
# If you wish to test other instructions, or with different values, you must add a new test case component to the circuit.
# If you do not do this, the tests will run sequentially, meaning the next test will use the CPU state obtained after executing the prior test.
# This is reflected below in the last test data row that checks if the program counter increased by 4.
init R3=9;

# WRITE R3, [R0 + 216]
0     0xe0d8300f 0      1  0  x           0          x
1     0xe0d8300f 0      x  x  x           x          x
0     0          0      0  1  9           0xd8       x
1     0          0      0  0  x           x          x

# Fetch next instruction, check if the program counter increased by 4...
0     0          0      1  0  x           4          x
*/

/* Test case write and read:
Clock Databus_in Halted RE WE Databus_out Addressbus R3
# The first line of test data must be the header, which contains the inputs and outputs used in the test case.
# It is possible to use registers in test cases by enabling their 'use as measurement value' attribute in the advanced tab.
# The R0-R15 registers have this attribute enabled in the provided template.

# These init statements are used to set the register contents when the simulation is started.
# Note that all init statements are collected and executed first. Interleaving them with regular test data has no effect.
# If you wish to test other instructions, or with different values, you must add a new test case component to the circuit.
# If you do not do this, the tests will run sequentially, meaning the next test will use the CPU state obtained after executing the prior test.
# This is reflected below in the last test data row that checks if the program counter increased by 4.
init R4=9;

# WRITE R4, [R0 + 216]
0     0xe0d8400f 0      1  0  x           0          x
1     0xe0d8400f 0      x  x  x           x          x
0     0          0      0  1  9           0xd8       x
1     0          0      0  0  x           x          x

# Fetch next instruction, check if the program counter increased by 4...
0     0          0      1  0  x           4          x

# READ [R0 + 216], R3
0     0xc0d8003f 0      1  0  x           4          x
1     0xc0d8003f 0      x  x  x           x          x
0     9          0      1  0  x           0xd8       x
1     0          0      0  0  x           x          9

0     0          0      1  0  x           8          9
*/

/* Test case loadhi:
Clock Databus_in Halted RE WE Databus_out Addressbus R2
# The first line of test data must be the header, which contains the inputs and outputs used in the test case.
# It is possible to use registers in test cases by enabling their 'use as measurement value' attribute in the advanced tab.
# The R0-R15 registers have this attribute enabled in the provided template.

# These init statements are used to set the register contents when the simulation is started.
# Note that all init statements are collected and executed first. Interleaving them with regular test data has no effect.
# If you wish to test other instructions, or with different values, you must add a new test case component to the circuit.
# If you do not do this, the tests will run sequentially, meaning the next test will use the CPU state obtained after executing the prior test.
# This is reflected below in the last test data row that checks if the program counter increased by 4.
init R1=4;
init R2=5;

# LOADHI 1, R2
# Machine code: 0x8000 012f
# The four test data lines below describe the testing of the LOADHI 1, R2 instruction.
# We first load the machine code into the Databus_in, and then drive the clock to step through the full instruction cycle once.
# Note that the first two columns (in this case) are inputs, meaning they will be set to the provided value.
# The other columns are outputs, which are evaluated after the inputs have been set, and then compared against the given expected values.
# The value 'x' denotes a 'do not care' value. Please click the 'Help' button in this dialog for more information regarding test cases.
0     0x8000012f 0      1  0  x           0          x
1     0x8000012f 0      x  x  x           x          x
0     0          0      0  0  x           x          x
1     0          0      0  0  x           x          1024

# Fetch next instruction, check if the program counter increased by 4...
0     0          0      1  0  x           4          x
*/

/* Test case arith2 sub:
Clock Databus_in Halted RE WE Databus_out Addressbus R3
# The first line of test data must be the header, which contains the inputs and outputs used in the test case.
# It is possible to use registers in test cases by enabling their 'use as measurement value' attribute in the advanced tab.
# The R0-R15 registers have this attribute enabled in the provided template.

# These init statements are used to set the register contents when the simulation is started.
# Note that all init statements are collected and executed first. Interleaving them with regular test data has no effect.
# If you wish to test other instructions, or with different values, you must add a new test case component to the circuit.
# If you do not do this, the tests will run sequentially, meaning the next test will use the CPU state obtained after executing the prior test.
# This is reflected below in the last test data row that checks if the program counter increased by 4.
init R1=4;
init R2=15;

# SUB 32, R2, R3
# Machine code: 0x7020 023f
# The four test data lines below describe the testing of the ADD R1, R2, R3 instruction.
# We first load the machine code into the Databus_in, and then drive the clock to step through the full instruction cycle once.
# Note that the first two columns (in this case) are inputs, meaning they will be set to the provided value.
# The other columns are outputs, which are evaluated after the inputs have been set, and then compared against the given expected values.
# The value 'x' denotes a 'do not care' value. Please click the 'Help' button in this dialog for more information regarding test cases.
0     0x7020023f 0      1  0  x           0          x
1     0x7020023f 0      x  x  x           x          x
0     0          0      0  0  x           x          x
1     0          0      0  0  x           x          (32-15)

# Fetch next instruction, check if the program counter increased by 4...
0     0          0      1  0  x           4          x
*/

/* Test case arith2 sub testfails:
Clock Databus_in Halted RE WE Databus_out Addressbus R3
# The first line of test data must be the header, which contains the inputs and outputs used in the test case.
# It is possible to use registers in test cases by enabling their 'use as measurement value' attribute in the advanced tab.
# The R0-R15 registers have this attribute enabled in the provided template.

# These init statements are used to set the register contents when the simulation is started.
# Note that all init statements are collected and executed first. Interleaving them with regular test data has no effect.
# If you wish to test other instructions, or with different values, you must add a new test case component to the circuit.
# If you do not do this, the tests will run sequentially, meaning the next test will use the CPU state obtained after executing the prior test.
# This is reflected below in the last test data row that checks if the program counter increased by 4.
init R1=4;
init R2=15;
init R3=0;

# SUB.F 32, R2, R3
# Machine code: 0x7020 023f
# The four test data lines below describe the testing of the ADD R1, R2, R3 instruction.
# We first load the machine code into the Databus_in, and then drive the clock to step through the full instruction cycle once.
# Note that the first two columns (in this case) are inputs, meaning they will be set to the provided value.
# The other columns are outputs, which are evaluated after the inputs have been set, and then compared against the given expected values.
# The value 'x' denotes a 'do not care' value. Please click the 'Help' button in this dialog for more information regarding test cases.
0     0x7020023e 0      1  0  x           0          0
1     0x7020023e 0      x  x  x           x          0
0     0x7020023e 0      1  0  x           4          0
1     0x7020023e 0      x  x  x           x          0

# Fetch next instruction, check if the program counter increased by 4...
0     0          0      1  0  x           8          x
*/
