// Digital circuit FlagRegisterBank.dig as structural Verilog
// The FlagRegisterBank component, which stores the current values of the overflow, negative, carry and zero flags.
module FlagRegisterBank (
  input  Carry_in,
  input  Overflow_in,
  input  Negative_in,
  input  Zero_in,
  input  Set,
  input  Clock,
  output Carry_out,
  output Overflow_out,
  output Negative_out,
  output Zero_out
);

  Register CARRY_BIT (.D(Carry_in), .C(Clock), .en(Set), .Q(Carry_out));
  Register OVERFLOW_BIT (.D(Overflow_in), .C(Clock), .en(Set), .Q(Overflow_out));
  Register NEGATIVE_BIT (.D(Negative_in), .C(Clock), .en(Set), .Q(Negative_out));
  Register ZERO_BIT (.D(Zero_in), .C(Clock), .en(Set), .Q(Zero_out));

  // Notes on the sheet:
  //   Carry_in: The input carry flag.
  //   Overflow_in: The input overflow flag.
  //   Negative_in: The input negative flag.
  //   Zero_in: The input zero flag.
  //   Carry_out: The current value of the stored carry flag.
  //   Overflow_out: The current value of the stored overflow flag.
  //   Negative_out: The current value of the stored negative flag.
  //   Zero_out: The current value of the stored zero flag.
  //   Set: If set to high and a rising clock edge occurs, the input flags will be stored in the respective flag registers.
endmodule
