// Digital circuit FormatDecoder.dig as structural Verilog
module FormatDecoder (
  input  [5:0] MSB6,
  output [2:0] FORMAT
);

  wire IS_ARITH2_eq, IS_ARITH3_eq, IS_HALT_eq, IS_LOADHI_eq, IS_READ_eq, IS_WRITE_eq;

  Comparator #(.Bits(6)) IS_HALT (.a({6{1'b1}}), .b(MSB6), .eq(IS_HALT_eq));  // open: gt, lt
  Comparator #(.Bits(6)) IS_WRITE (.a(6'b111000), .b(MSB6), .eq(IS_WRITE_eq));  // open: gt, lt
  Comparator #(.Bits(6)) IS_READ (.a(6'b110000), .b(MSB6), .eq(IS_READ_eq));  // open: gt, lt
  Comparator #(.Bits(2)) IS_LOADHI (.a(2'b10), .b(MSB6[5:4]), .eq(IS_LOADHI_eq));  // open: gt, lt
  Comparator #(.Bits(2)) IS_ARITH3 (.a(2'b01), .b({MSB6[5], MSB6[0]}), .eq(IS_ARITH3_eq));  // open: gt, lt
  Comparator #(.Bits(2)) IS_ARITH2 (.a(2'b00), .b({MSB6[5], MSB6[0]}), .eq(IS_ARITH2_eq));  // open: gt, lt
  PriorityEncoder #(.Selector_Bits(3)) FORMAT_ENCODER (
    .in0(1'b0), .in1(IS_HALT_eq), .in2(IS_WRITE_eq), .in3(IS_READ_eq), .in4(IS_LOADHI_eq),
    .in5(IS_ARITH3_eq), .in6(IS_ARITH2_eq), .in7(1'b0), .num(FORMAT));  // open: any

  // Notes on the sheet:
  //   MSB6: input: 6 most significant bits
  //   FORMAT: Format 1-6
endmodule

/* Test case recognisesFormat:
           MSB6 	FORMAT


repeat(16) (2*n+1) 	(5)
repeat(16) (2*n)   	(6)
repeat(16) (n+32)	(4)
           (0b110000) 	(3)
           (0b111000) 	(2)
           (0b111111) 	(1)
*/
