// Digital circuit InstructionDecoder.dig as structural Verilog
// The InstructionDecoder component, which serves as a hub to control many of the signals to other components. It implements both the fetch operation, and execution of machine code (including decoding).
module InstructionDecoder (
  input  [31:0] Instruction,
  input  Fetch,
  input  Execute,
  input  Clock,
  output [3:0] Reg_dest,
  output [3:0] Reg_B,
  output [3:0] Reg_A,
  output [2:0] Opcode,
  output [3:0] Condition,
  output SetFlag,
  output [31:0] Constant,
  output Halt,
  output WE,
  output RE,
  output LOADHI,
  output ARITH2,
  output ARITH3
);

  wire decoder_1_out_3, decoder_1_out_6, or_3_out;
  wire [2:0] formatdecoder_1_format;
  wire [3:0] multiplexer_1_out;
  wire [31:0] C10_to_C32_out, multiplexer_4_out;
  wire [31:4] IR_q, multiplexer_1_out_2;

  Register #(.Bits(32)) IR (.D(Instruction), .C(Clock), .en(Fetch), .Q({IR_q, Condition}));
  Multiplexer #(.Bits(32)) multiplexer_1 (
    .sel(Execute), .in_0({32{1'b0}}), .in_1({IR_q, Condition}),
    .out({multiplexer_1_out_2[31:28], SetFlag, multiplexer_1_out_2[26:16], Reg_A, multiplexer_1_out_2[11:4], multiplexer_1_out}));
  BitExtender #(.inputBits(10), .outputBits(32)) C10_to_C32 (.in(multiplexer_1_out_2[25:16]), .out(C10_to_C32_out));
  FormatDecoder formatdecoder_1 (
    .MSB6({multiplexer_1_out_2[31:28], SetFlag, multiplexer_1_out_2[26]}), .FORMAT(formatdecoder_1_format));
  Decoder #(.Selector_Bits(3)) decoder_1 (
    .sel(formatdecoder_1_format), .out_1(Halt), .out_2(WE), .out_3(decoder_1_out_3), .out_4(LOADHI),
    .out_5(ARITH3), .out_6(decoder_1_out_6));  // open: out_0, out_7
  or or_1 (RE, decoder_1_out_3, Fetch);
  Multiplexer #(.Bits(4)) multiplexer_2 (.sel(Fetch), .in_0(multiplexer_1_out_2[11:8]), .in_1(4'b1111), .out(Reg_B));
  Multiplexer #(.Bits(4)) multiplexer_3 (.sel(Fetch), .in_0(multiplexer_1_out_2[7:4]), .in_1(4'b1111), .out(Reg_dest));
  Multiplexer #(.Bits(32)) multiplexer_4 (
    .sel(LOADHI), .in_0(C10_to_C32_out),
    .in_1({multiplexer_1_out_2[29:28], SetFlag, multiplexer_1_out_2[26:16], Reg_A, multiplexer_1_out_2[11:8], {10{1'b0}}}),
    .out(multiplexer_4_out));
  Multiplexer #(.Bits(32)) multiplexer_5 (.sel(Fetch), .in_0(multiplexer_4_out), .in_1(32'h4), .out(Constant));
  or or_2 (ARITH2, decoder_1_out_6, Fetch);
  or or_3 (or_3_out, WE, decoder_1_out_3, Fetch);
  Multiplexer #(.Bits(3)) multiplexer_6 (
    .sel(or_3_out), .in_0(multiplexer_1_out_2[30:28]), .in_1(3'b110), .out(Opcode));

  // Notes on the sheet:
  //   Instruction: The instruction machine code input. If the CPU is in the fetch phase and a rising clock signal occurs, this machine code is stored in the internal instruction register (IR), so that it can be decoded and executed.
  //   Reg_dest: Destination register output, which determines the register that should store the result of a data operation. A data operation is either an ALU computation, or a read from an external device, such as RAM.
  //   Reg_B: B register output, which determines the register to be used for the second operand.
  //   Reg_A: A register output, which determines the register to be used for the first operand.
  //   Opcode: Opcode output, which determines the operation the ALU should perform.
  //   Condition: Instruction condition output, which contains the condition under which the instruction should be executed.
  //   Fetch: Enables Instruction to set content of Instruction Register (IR)
  //   Halt: If true, the instruction format was HALT.
  //   Execute: Enables all outputs other than Condition. Condition is always enabled.
  //   In fetch phase, the instruction
  //   decoder simultaneously issues an
  //   ADD 4, R16, R16 and also 
  //   splits the current value of R16 to
  //   the databus_OUT, issueing a read
endmodule
