// Digital circuit OverflowSubtract.dig as structural Verilog
module OverflowSubtract (
  input  [31:0] A,
  input  [31:0] B,
  input  [31:0] Result,
  output O
);

  wire msb_1_o, msb_2_o, msb_3_o, not_1_out, xnor_1_out, xnor_2_out;

  MSB msb_1 (.A(Result), .O(msb_1_o));
  MSB msb_2 (.A(B), .O(msb_2_o));
  MSB msb_3 (.A(A), .O(msb_3_o));
  xnor xnor_1 (xnor_1_out, msb_1_o, msb_2_o);
  not not_1 (not_1_out, msb_1_o);
  xnor xnor_2 (xnor_2_out, not_1_out, msb_3_o);
  and and_1 (O, xnor_1_out, xnor_2_out);
endmodule
